# Fritzing sketch batteries-sketch-1.0 (saved by Fritzing 0.9.3b)
breadboards: 2

parts:
  Batteries = Battery
  LED4 = LED - 5mm [color="Yellow (595nm)" package="5 mm [THT]"]
  U4 = NodeMCU V3.0
  SERVO3 = Tower Pro SG90 servo [part_number=101246]

nets:
  N1: Batteries.-, LED4.cathode, U4.GND#6, U4.GND#13, U4.GND#16, U4.GND#33, SERVO3.GND
  N2: Batteries.+, U4.3V3
  N3: LED4.anode, U4.D5
  N4: U4.D1, SERVO3.Signal
  VIN: U4.Vin, SERVO3.+5V

custom parts:
  Battery: Your standard 2x 18650 battery pack (14.7 Volts)
  NodeMCU V3.0: ESP8266 based NodeMCU
  Tower Pro SG90 servo: Original file by John De Cristofaro http://www.adafruit.com/products/1449 Adafruit Feedback Servo (Small) Edited by: e-radionica.com 28/9/2015
