# Fritzing sketch batteries-sketch-1.1 (saved by Fritzing 0.9.3b)
breadboards: 2

parts:
  Batteries = Battery
  LED4 = LED - 5mm [color="Yellow (595nm)" package="5 mm [THT]"]
  U4 = NodeMCU V3.0
  SERVO3 = Tower Pro SG90 servo [part_number=101246]
  Part4 = BH1750

nets:
  N1: Batteries.-, LED4.cathode, U4.GND#6, U4.GND#13, U4.GND#16, U4.GND#33, Part4.GND
  3V3: Batteries.+, U4.3V3, Part4.VCC
  N2: LED4.anode, U4.D5
  N3: U4.D1, SERVO3.Signal
  N4: U4.D3, Part4.SDA, Part4.ADDR
  N5: U4.D4, Part4.SCL
  N6: U4.VU, SERVO3.+5V
  N7: U4.GND#41, SERVO3.GND

custom parts:
  Battery: Your standard 2x 18650 battery pack (14.7 Volts)
  NodeMCU V3.0: ESP8266 based NodeMCU
  Tower Pro SG90 servo: Original file by John De Cristofaro http://www.adafruit.com/products/1449 Adafruit Feedback Servo (Small) Edited by: e-radionica.com 28/9/2015
  BH1750: Light Sensor
