# Fritzing sketch batteries-sketch-2.0 (saved by Fritzing 0.9.3b)
breadboards: 2

parts:
  LED4 = LED - 5mm [color="Yellow (595nm)" package="5 mm [THT]"]
  U4 = NodeMCU V3.0
  SERVO3 = Tower Pro SG90 servo [part_number=101246]
  SERVO4 = Tower Pro SG90 servo [part_number=101246]
  Batteries1 = Battery

nets:
  GND: LED4.cathode, U4.GND#6, U4.GND#13, U4.GND#16, U4.GND#33, SERVO3.GND, SERVO4.GND, Batteries1.-
  N1: LED4.anode, U4.D5
  N2: U4.D1, SERVO3.Signal
  N3: U4.D2, SERVO4.Signal
  3V3: U4.3V3, SERVO4.+5V, Batteries1.+
  VIN: U4.Vin, SERVO3.+5V

custom parts:
  NodeMCU V3.0: ESP8266 based NodeMCU
  Tower Pro SG90 servo: Original file by John De Cristofaro http://www.adafruit.com/products/1449 Adafruit Feedback Servo (Small) Edited by: e-radionica.com 28/9/2015
  Battery: Your standard 2x 18650 battery pack (14.7 Volts)
